# Fritzing sketch OpenSensor (saved by Fritzing 1.0.4)

parts:
  A1 = ESP32-S3-WROOM-1-N16R8 dev board
  M1 = ph-4502c [package=THT]
  Part1 = ADS1115

nets:
  N1: A1.Pin_12, Part1.SDA
  N2: A1.Pin_15, Part1.SCL
  N3: A1.Pin_21, M1.pin6, Part1.VDD
  N4: A1.Pin_22, M1.pin5, Part1.GND
  N5: M1.pin3, Part1.A0

notes:
  SDA
  SCL

custom parts:
  ESP32-S3-WROOM-1-N16R8 dev board: ESP32-S3 WIFI+BLE5.0 Development Board ESP32-S3-WROOM-1-N16R8(16M Flash/8SRAM).
  ph-4502c: ph-4502c PH Meter.
  ADS1115: ADC ADS1115

// code stored in the sketch: old.ino
#static const uint8_t SDA = 8;
#static const uint8_t SCL = 9;
